# Fritzing sketch APWCR_Wire_Layout_MEGA+Pi5 (saved by Fritzing 1.0.6)
breadboards: 1

parts:
  J1 = Basic Servo
  J2 = Basic Servo
  U1 = LIPO-2000mAh [package=lipo-2000]
  U2 = LIPO-2000mAh [package=lipo-2000]
  A1 = Raspberry Pi 5  # not connected
  DC_Mot_Enc1 = DC Motor with two-phase hall-encoder [part_number=VT-E-G25A-06-177E]
  DC_Mot_Enc2 = DC Motor with two-phase hall-encoder [part_number=VT-E-G25A-06-177E]
  DC_Mot_Enc3 = DC Motor with two-phase hall-encoder [part_number=VT-E-G25A-06-177E]
  DC_Mot_Enc4 = DC Motor with two-phase hall-encoder [part_number=VT-E-G25A-06-177E]
  A2 = XY-3606
  A3 = XY-3606
  J3 = Screw terminal - 2 pins [package=THT]
  A4 = XY-3606
  Part4 = Adafruit DRV8871 [part_number="Adafruit #3190"]
  Part5 = Adafruit DRV8871 [part_number="Adafruit #3190"]
  Part6 = Adafruit DRV8871 [part_number="Adafruit #3190"]
  Part7 = Adafruit DRV8871 [part_number="Adafruit #3190"]
  J4 = Screw terminal - 2 pins [package=THT]
  J5 = Screw terminal - 2 pins [package=THT]
  J6 = Screw terminal - 2 pins [package=THT]
  J7 = Screw terminal - 2 pins [package=THT]
  J8 = Screw terminal - 2 pins [package=THT]
  Part8 = Arduino Mega 2560 (Rev3)
  Part9 = SRF05 Ultrasonic Rangefinder
  J9 = Basic Servo

nets:
  N1: J1.gnd, A3.Pin_2, A3.Pin_3, J6.pin2, J7.pin2
  N2: J1.vcc, A3.Pin_4, J6.pin1, J7.pin1
  N3: J1.pulse, Part8.A1
  N4: J2.pulse, Part8.A0
  N5: U1.+, A2.Pin_1
  N6: U1.-, A2.Pin_2
  N7: U2.+, J3.pin1, A4.Pin_1, Part4.VMOTOR, J4.pin2
  GND: U2.-, DC_Mot_Enc1.pin4, J3.pin2, A4.Pin_2, A4.Pin_3, Part4.GND, J4.pin1, J5.pin2, J8.pin2, Part8.GND
  N8: DC_Mot_Enc1.pin1, Part4.OUT2
  N9: DC_Mot_Enc1.pin2, Part4.OUT1
  N10: DC_Mot_Enc1.pin3, Part8.D2_PWM
  N11: DC_Mot_Enc1.pin5, A4.Pin_4, J5.pin1, J8.pin1
  N12: DC_Mot_Enc1.pin6, Part8.D20/SDA, Part8.SDA
  N13: DC_Mot_Enc2.pin1, Part7.OUT2
  N14: DC_Mot_Enc2.pin2, Part7.OUT1
  N15: DC_Mot_Enc2.pin3, Part8.D19/RX1
  N16: DC_Mot_Enc2.pin6, Part8.D23
  N17: DC_Mot_Enc3.pin1, Part5.OUT2
  N18: DC_Mot_Enc3.pin2, Part5.OUT1
  N19: DC_Mot_Enc3.pin3, Part8.D3_PWM
  N20: DC_Mot_Enc3.pin6, Part8.D21/SCL, Part8.SCL
  N21: DC_Mot_Enc4.pin1, Part6.OUT2
  N22: DC_Mot_Enc4.pin2, Part6.OUT1
  N23: DC_Mot_Enc4.pin3, Part8.D18/TX1
  N24: DC_Mot_Enc4.pin6, Part8.D22
  N25: Part4.IN1, Part8.D4_PWM
  N26: Part4.IN2, Part8.D5_PWM
  N27: Part5.IN1, Part8.D13_PWM
  N28: Part5.IN2, Part8.D6_PWM
  N29: Part6.IN1, Part8.D11_PWM
  N30: Part6.IN2, Part8.D9_PWM
  N31: Part7.IN1, Part8.D12_PWM
  N32: Part7.IN2, Part8.D10_PWM
  N33: Part8.A2, J9.pulse
  N34: Part8.D8_PWM, Part9.Trig
  N35: Part8.D7_PWM, Part9.Echo

notes:
  Raspberry Pi 5 / High-Level Computer
  Arduino Mega
  12/24V to 5V/5A Buck Convertor to USB-C Output
  12/24V to 5V 5A Buck Convertor - Servo Power
  12/24V to 5V 5A Buck Convertor - Logic Power
  3S (12V) LiPo Battery - Motors/Actuation
  3S (12V) LiPo Battery - Computing
  MG996R Servo
  LHS Drive Motor
  Power Distribution Board
  USB-USBC Cable
  USB Cable
  DRV8871 Motor Drivers
  (Yellow Encoder Wire = Quad Encoder A Signal)
  (Blue/Green Encoder Wire = Encoder +5Vcc/Ground)
  RHS Drive Motor
  LHS WC Motor
  RHS WC Motor
  (Gray Encoder Wire = Quad Encoder B Signal)
  (IN2 Wire = PWM)
  (IN2 Wire = PH/Direction)
  HC-SR04 Dist SNSR

custom parts:
  Raspberry Pi 5: The RPi5, a faster version of the awesome Raspberry Pi4B ARM Board with 40 pin gpio.
  XY-3606: 24V/12V turn 5V 5A power module, DC-DC XY-3606 Power Converter Super LM2596S.
  Adafruit DRV8871: Crank up your robotics with powerful Adafruit DRV8871 motor driver breakout board. This motor driver has a lot of great specs that make it useful for a wide variety of mechatronics. In particular, the simple resistor-set current limiting and auto-magic PWM support make it super easy to use. Check out the specs for the DRV8871: 6.5V to 45V motor power voltage Up to 5.5V logic level on IN pins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
